// Logisim project hierarchy_control.circ as structural Verilog: 2 circuits, main circuit hier4
module buffer4 (
  input  [3:0] A,
  output [3:0] Y
);


  assign Y = A;

  // Other names for the same wires on the sheet: bit_1 = A[0]; bus_5[3:0] = A; bit_2 = A[1]; bit_3 = A[2];
  //   bit_4 = A[3]
endmodule

module hier4 (
  input  [3:0] A,
  output [3:0] Y
);

  buffer4 buffer4_1 (.A(A), .Y(Y));

  // Other names for the same wires on the sheet: buffer4_Y_1[3:0] = Y
endmodule
