// Logisim project tutorial_missing_output_fault.circ as structural Verilog: 1 circuit, main circuit tutorial_gui
module tutorial_gui (
  input  X,
  input  Y,
  output Z
);

  wire and_1_out, and_2_out, not_1_out, not_2_out;

  not not_1 (not_1_out, X);
  not not_2 (not_2_out, Y);
  and and_1 (and_1_out, X, not_2_out);
  and and_2 (and_2_out, not_1_out, Y);
  // OR_Gate or_1 has open pins: in0=and_1_out, in1=and_2_out, out=open
endmodule
